# Fritzing sketch ld2410wiringdiagram (saved by Fritzing 0.9.4)
breadboards: 1

parts:
  A1 = Hi-link-HLK-LD2410_1
  Mod2 = Raspberry Pi Pico W
  OLED1 = SSD1306 0.96in 128x64 I2C Monochrome OLED Display

nets:
  N1: A1.connector1, Mod2.pin_27
  N2: A1.connector2, Mod2.pin_26
  N3: A1.connector3, Mod2.pin_3, Mod2.pin_8, Mod2.pin_13, Mod2.pin_18, Mod2.pin_23, Mod2.pin_28, Mod2.pin_33, Mod2.pin_38, Mod2.pin_42, OLED1.GND
  N4: A1.connector4, Mod2.pin_40
  N5: Mod2.pin_21, OLED1.SDA
  N6: Mod2.pin_22, OLED1.SCL
  N7: Mod2.pin_36, OLED1.VCC

custom parts:
  Raspberry Pi Pico W: Raspberry Pi Pico W. Based around the RP2040 microcontroller the Pico W is a low cost microcontroller device bringing Raspberry Pi quality, cost, and easy of use to the microcontroller space. The areas marked KEEPOUT in pcb silkscreen should not have traces running through them to avoid shorts on a soldered in module!
