# Fritzing sketch LDR Demo (saved by Fritzing 0.9.4)
breadboards: 1

parts:
  OLED1 = SSD1306 0.96in 128x64 I2C Monochrome OLED Display  # not connected
  Mod1 = Raspberry Pi Pico W
  R1 = Photocell (LDR) [package=THT]
  R2 = Resistor [tolerance=±5% resistance=220 package=THT]
  LED1 = smd LED [color="Green (555nm)" package="0603 [SMD]"]
  LED2 = smd LED [color="Red (633nm)" package="0603 [SMD]"]
  LED3 = smd LED [color="Yellow (595nm)" package="0603 [SMD]"]

nets:
  N1: Mod1.pin_3, Mod1.pin_8, Mod1.pin_13, Mod1.pin_18, Mod1.pin_23, Mod1.pin_28, Mod1.pin_33, Mod1.pin_38, Mod1.pin_42, R2.Pin_0, LED1.cathode, LED2.cathode, LED3.cathode
  N2: Mod1.pin_17, LED1.anode
  N3: Mod1.pin_19, LED3.anode
  N4: Mod1.pin_20, LED2.anode
  N5: Mod1.pin_31, R1.pin_0, R2.Pin_1
  N6: Mod1.pin_36, R1.pin_1

custom parts:
  Raspberry Pi Pico W: Raspberry Pi Pico W. Based around the RP2040 microcontroller the Pico W is a low cost microcontroller device bringing Raspberry Pi quality, cost, and easy of use to the microcontroller space. The areas marked KEEPOUT in pcb silkscreen should not have traces running through them to avoid shorts on a soldered in module!
