# Fritzing sketch boilerroom (saved by Fritzing 0.9.4)
breadboards: 1

parts:
  Mod1 = Raspberry Pi Pico W
  DHT1 = DHT11 Humitidy and Temperature Sensor (3 pins)
  LED1 = LED - 3mm [color="Red (633nm)" package="3 mm [THT]"]
  S1 = Momentary Switch [package=ksa_sealed_tac_switch]

nets:
  N1: Mod1.pin_3, Mod1.pin_8, Mod1.pin_13, Mod1.pin_18, Mod1.pin_23, Mod1.pin_28, Mod1.pin_33, Mod1.pin_38, DHT1.Gnd, S1.1
  N2: Mod1.pin_17, S1.4
  N3: Mod1.pin_20, LED1.anode
  N4: Mod1.pin_21, DHT1.Plus
  N5: Mod1.pin_36, DHT1.Signal, LED1.cathode

custom parts:
  Raspberry Pi Pico W: Raspberry Pi Pico W. Based around the RP2040 microcontroller the Pico W is a low cost microcontroller device bringing Raspberry Pi quality, cost, and easy of use to the microcontroller space. The areas marked KEEPOUT in pcb silkscreen should not have traces running through them to avoid shorts on a soldered in module!
  DHT11 Humitidy and Temperature Sensor (3 pins): DHT11 Humidity and Temperature Sensor (3 pins).
