# Fritzing sketch boilerroomalarm (saved by Fritzing 0.9.4)
breadboards: 1

parts:
  Mod1 = Raspberry Pi Pico W
  LED1 = LED - 3mm [color="Red (633nm)" package="3 mm [THT]"]
  OLED1 = SSD1306 0.96in 128x64 I2C Monochrome OLED Display
  J1 = Piezo Speaker
  LED3 = LED - 3mm [color="Blue (525nm)" package="3 mm [THT]"]
  LED4 = LED - 3mm [color="Green (570nm)" package="3 mm [THT]"]

nets:
  N1: Mod1.pin_3, Mod1.pin_8, Mod1.pin_13, Mod1.pin_18, Mod1.pin_23, Mod1.pin_28, Mod1.pin_33, Mod1.pin_38, LED1.cathode, OLED1.VCC, J1.pin1, LED3.cathode, LED4.cathode
  N2: Mod1.pin_19, J1.pin2
  N3: Mod1.pin_20, LED1.anode
  N4: Mod1.pin_21, OLED1.SDA
  N5: Mod1.pin_22, OLED1.SCL
  N6: Mod1.pin_24, LED4.anode
  N7: Mod1.pin_25, LED3.anode
  N8: Mod1.pin_36, OLED1.GND

custom parts:
  Raspberry Pi Pico W: Raspberry Pi Pico W. Based around the RP2040 microcontroller the Pico W is a low cost microcontroller device bringing Raspberry Pi quality, cost, and easy of use to the microcontroller space. The areas marked KEEPOUT in pcb silkscreen should not have traces running through them to avoid shorts on a soldered in module!
