# Fritzing sketch robotwithvoltagedivider (saved by Fritzing 0.9.4)
breadboards: 1

parts:
  Mod1 = Raspberry Pi Pico W
  L298N1 = L298N DC motor driver
  M1 = DC Motor
  M2 = DC Motor
  S1 = Momentary Switch [package=ksa_sealed_tac_switch]
  S2 = Momentary Switch [package=ksa_sealed_tac_switch]
  J1 = Basic Servo
  HC-SR04_Sensor_1 = HC-SR04 Ultrasonic Distance Sensor
  LED1 = smd LED [color="Red (633nm)" package="0805 [SMD]"]
  VCC1 = Battery  # not connected
  R1 = Resistor [tolerance=±5% resistance=220 package="0402 [SMD]"]
  R2 = Resistor [tolerance=±5% resistance=220 package="2512 [SMD]"]

nets:
  GND: Mod1.pin_3, Mod1.pin_8, Mod1.pin_13, Mod1.pin_18, Mod1.pin_23, Mod1.pin_28, Mod1.pin_33, Mod1.pin_38, Mod1.pin_42, L298N1.GND, S1.3, S1.4, S2.3, S2.4, J1.gnd, HC-SR04_Sensor_1.GND, LED1.cathode
  N1: Mod1.pin_5, HC-SR04_Sensor_1.TRIG
  N2: Mod1.pin_6, R1.Pin_0, R2.Pin_1
  N3: Mod1.pin_10, LED1.anode
  N4: Mod1.pin_14, L298N1.ENB
  N5: Mod1.pin_15, L298N1.IN4
  N6: Mod1.pin_16, L298N1.IN3
  N7: Mod1.pin_17, L298N1.IN2
  N8: Mod1.pin_19, L298N1.IN1
  N9: Mod1.pin_20, L298N1.ENA
  N10: Mod1.pin_21, J1.pulse
  N11: Mod1.pin_22, S1.1, S1.2
  N12: Mod1.pin_25, S2.1, S2.2
  VCC: Mod1.pin_40, J1.vcc, HC-SR04_Sensor_1.VCC
  N13: L298N1.OUT1, M2.pin_2
  N14: L298N1.OUT2, M2.pin_1
  N15: L298N1.OUT3, M1.pin_2
  N16: L298N1.OUT4, M1.pin_1
  N17: HC-SR04_Sensor_1.ECHO, R1.Pin_1

custom parts:
  Raspberry Pi Pico W: Raspberry Pi Pico W. Based around the RP2040 microcontroller the Pico W is a low cost microcontroller device bringing Raspberry Pi quality, cost, and easy of use to the microcontroller space. The areas marked KEEPOUT in pcb silkscreen should not have traces running through them to avoid shorts on a soldered in module!
  L298N DC motor driver: 2x DC motor driver with 78M05 positive voltage regulator (7..35 V) L298N: max 46 V, 2 A Set 5 V Enable jumper to enable 5 V regultor (needed for the L298N) and +5 V output at screw terminal or supply external +5 V at screw terminal Set ENA and/or ENB to +5 V to enable motor permanently or supply ENA and/or ENB with PWM signal IN1 and IN2 set rotation directory for motor A (OUT1/OUT2) IN2 and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
